# Fritzing sketch Calculator (saved by Fritzing 0.9.4)
breadboards: 1
perfboards: 1

parts:
  U2 = atmega328 [package=dip]
  XTAL1 = Crystal [frequency="16 Mhz" package=THT]
  LCD1 = LCD screen  # not connected
  S1 = Pushbutton [package="[THT]"]
  S2 = Pushbutton [package="[THT]"]  # not connected
  S3 = Pushbutton [package="[THT]"]
  S4 = Pushbutton [package="[THT]"]  # not connected
  S5 = Pushbutton [package="[THT]"]  # not connected
  S6 = Pushbutton [package="[THT]"]
  S7 = Pushbutton [package="[THT]"]
  S11 = Pushbutton [package="[THT]"]
  S12 = Pushbutton [package="[THT]"]  # not connected
  S13 = Pushbutton [package="[THT]"]
  S14 = Pushbutton [package="[THT]"]
  S15 = Pushbutton [package="[THT]"]
  S16 = Pushbutton [package="[THT]"]
  S17 = Pushbutton [package="[THT]"]
  S18 = Pushbutton [package="[THT]"]  # not connected
  S19 = Pushbutton [package="[THT]"]

nets:
  N1: U2.XLAT1, XTAL1.pin_0
  N2: U2.D5_(PWM), XTAL1.pin_1
  N3: S1.Pin_1, S1.Pin_2
  N4: S3.Pin_3, S3.Pin_4
  N5: S6.Pin_1, S6.Pin_2
  N6: S6.Pin_3, S6.Pin_4
  N7: S7.Pin_1, S7.Pin_2
  N8: S7.Pin_3, S7.Pin_4
  N9: S11.Pin_3, S11.Pin_4
  N10: S13.Pin_1, S13.Pin_2
  N11: S14.Pin_1, S14.Pin_2
  N12: S14.Pin_3, S14.Pin_4
  N13: S15.Pin_3, S15.Pin_4
  N14: S16.Pin_1, S16.Pin_2
  N15: S17.Pin_1, S17.Pin_2
  N16: S19.Pin_1, S19.Pin_2
